# Fritzing sketch Motor Driver (saved by Fritzing 0.9.0b)
breadboards: 1

parts:
  Q1 = NPN-Transistor [package="TO92 [THT]"]
  U1 = Vibration Motor- ROB-08449 [package=vibe-motor-10mm]
  R1 = Resistor [package="2010 [SMD]"]

nets:
  N1: Q1.E, U1.-
  N2: Q1.B, R1.Pin_0

notes:
  PWM
  VCC
  GND
  Motor Driver circuit
