# Fritzing sketch OFF switch (saved by Fritzing 0.9.0b)

parts:
  S1 = Pushbutton [package="[SMD]"]
  R1 = Resistor [package="2010 [SMD]"]
  U1 = atmega328 [package=dip]
  C1 = Capacitor [package=cap-pth-small2]

nets:
  N1: S1.Pin_1, S1.Pin_2, R1.Pin_0, U1.D2, C1.2
  N2: S1.Pin_3, S1.Pin_4, U1.GND, C1.1
  N3: R1.Pin_1, U1.D4

notes:
  VCC
  GND
  INT0
  pullup
  ESP8266 RST
  ON/OFF Switch
  On Switch press, atmega328 puts ESP8266 in deep sleep through AT cmd
  Then, Atmega328 itself goes into sleep mode that can be woken up by an external INT0
